// Logisim project newcpu.circ as structural Verilog: 22 circuits, main circuit main
module Flag_Selector (
  input  F,
  input  E,
  output Q,
  output Q_prime
);

  assign Q = E ? F : 1'bz;  // Controlled_Buffer controlled_buffer_1
  assign Q_prime = E ? ~F : 1'bz;  // Controlled_Inverter controlled_inverter_1
endmodule

module Floating_1 (
  input  D,
  output Q
);

  assign Q = D ? D : 1'bz;  // Controlled_Buffer controlled_buffer_1
endmodule

module Rising_Edge_Detector (
  input  in_1,
  output out_2
);

  wire not_1_out, not_2_out, not_3_out;

  not not_1 (not_1_out, in_1);
  not not_2 (not_2_out, not_1_out);
  and and_1 (out_2, in_1, not_3_out);
  not not_3 (not_3_out, not_2_out);
endmodule

// SR
module CD4043BE (
  input  [3:0] S,
  input  E,
  input  [3:0] R,
  output [3:0] Q
);

  S_R_Flip_Flop #(.trigger("low")) s_r_ff_1 (
    .S(S[0]), .clk(1'b0), .R(R[0]), .Q(Q[0]), .preset(1'b0), .reset(1'b0), .en(E));  // open: Qn
  S_R_Flip_Flop #(.trigger("low")) s_r_ff_2 (
    .S(S[1]), .clk(1'b0), .R(R[1]), .Q(Q[1]), .preset(1'b0), .reset(1'b0), .en(E));  // open: Qn
  S_R_Flip_Flop #(.trigger("low")) s_r_ff_3 (
    .S(S[2]), .clk(1'b0), .R(R[2]), .Q(Q[2]), .preset(1'b0), .reset(1'b0), .en(E));  // open: Qn
  S_R_Flip_Flop #(.trigger("low")) s_r_ff_4 (
    .S(S[3]), .clk(1'b0), .R(R[3]), .Q(Q[3]), .preset(1'b0), .reset(1'b0), .en(E));  // open: Qn
endmodule

module CD74HC670E (
  input  [3:0] D,
  input  WA0,
  input  WA1,
  input  WE_prime,
  input  RE_prime,
  input  RA1,
  input  RA0,
  output [3:0] Q,
  output [3:0] F
);

  wire decoder_1_out0, decoder_1_out1, decoder_1_out2, decoder_1_out3, decoder_2_out0, decoder_2_out1,
       decoder_2_out2, decoder_2_out3, not_1_out, not_2_out;
  wire [3:0] register_1_q, register_2_q, register_3_q;

  Decoder #(.select(2), .disabled(0)) decoder_1 (
    .out0(decoder_1_out0), .out1(decoder_1_out1), .out2(decoder_1_out2), .out3(decoder_1_out3),
    .sel({WA1, WA0}), .en(not_1_out));
  Decoder #(.select(2), .disabled(0)) decoder_2 (
    .out0(decoder_2_out0), .out1(decoder_2_out1), .out2(decoder_2_out2), .out3(decoder_2_out3),
    .sel({RA1, RA0}), .en(not_2_out));
  Register #(.width(4)) register_1 (.D(D), .en(not_1_out), .Q(register_1_q), .clk(decoder_1_out0), .clr(1'b0));
  assign Q = decoder_2_out0 ? register_1_q : 4'bz;  // Controlled_Buffer controlled_buffer_1
  Register #(.width(4)) register_2 (.D(D), .en(not_1_out), .Q(register_2_q), .clk(decoder_1_out2), .clr(1'b0));
  assign Q = decoder_2_out1 ? register_3_q : 4'bz;  // Controlled_Buffer controlled_buffer_2
  Register #(.width(4)) register_3 (.D(D), .en(not_1_out), .Q(register_3_q), .clk(decoder_1_out1), .clr(1'b0));
  assign Q = decoder_2_out2 ? register_2_q : 4'bz;  // Controlled_Buffer controlled_buffer_3
  Register #(.width(4)) register_4 (.D(D), .en(not_1_out), .Q(F), .clk(decoder_1_out3), .clr(1'b0));
  not not_1 (not_1_out, WE_prime);
  not not_2 (not_2_out, RE_prime);
  assign Q = decoder_2_out3 ? F : 4'bz;  // Controlled_Buffer controlled_buffer_4
endmodule

module CD74HCT573E (
  input  OE_prime,
  input  Vcc,
  input  [7:0] D,
  input  GND,
  input  LE_prime,
  output [7:0] Q
);

  wire not_1_out, not_2_out;
  wire [7:0] register_1_q;

  not not_1 (not_1_out, OE_prime);
  Register register_1 (.D(D), .en(Vcc), .Q(register_1_q), .clk(not_2_out), .clr(GND));
  assign Q = not_1_out ? register_1_q : 8'bz;  // Controlled_Buffer controlled_buffer_1
  not not_2 (not_2_out, LE_prime);
  // also tied to GND on the sheet: GND
  // also tied to VCC on the sheet: Vcc
endmodule

module SN74F283N (
  input  Vcc,
  input  B2,
  input  B3,
  input  A2,
  input  A3,
  input  B1,
  input  B4,
  input  A1,
  input  A4,
  input  CI,
  input  GND,
  output Q2,
  output Q1,
  output Q3,
  output Q4,
  output CO
);

  Adder #(.width(4)) adder_1 (.a({B4, B3, B2, B1}), .b({A4, A3, A2, A1}), .out({Q4, Q3, Q2, Q1}), .cin(CI), .cout(CO));
  // also tied to GND on the sheet: GND
  // also tied to VCC on the sheet: Vcc
endmodule

// AND
module SN74HC08BN (
  input  A0,
  input  Vcc,
  input  B0,
  input  A2,
  input  B2,
  input  A1,
  input  B1,
  input  A3,
  input  in_9,
  input  GND,
  output Q0,
  output Q2,
  output Q1,
  output Q3
);

  and and_1 (Q0, B0, A0);
  and and_2 (Q2, A2, B2);
  and and_3 (Q1, B1, A1);
  and and_4 (Q3, A3, in_9);
  // also tied to GND on the sheet: GND
  // also tied to VCC on the sheet: Vcc
endmodule

module SN74HC595N (
  input  Vcc,
  input  GND,
  input  SER,
  input  OE_prime,
  input  RCLK,
  input  SRCLK,
  input  SRCLR_prime,
  output [7:0] Q,
  output Qh_prime
);

  wire not_1_out, not_2_out, shift_register_1_out;
  wire [7:0] register_1_q, shift_register_1_q0;

  assign Q = not_1_out ? register_1_q : 8'bz;  // Controlled_Buffer controlled_buffer_1
  Shift_Register shift_register_1 (
    .shift(Vcc), .in(SER), .clk(SRCLK), .out(shift_register_1_out), .load(GND), .clr(not_2_out), .d0(GND),
    .q0(shift_register_1_q0[0]), .d1(GND), .q1(shift_register_1_q0[1]), .d2(GND),
    .q2(shift_register_1_q0[2]), .d3(GND), .q3(shift_register_1_q0[3]), .d4(GND),
    .q4(shift_register_1_q0[4]), .d5(GND), .q5(shift_register_1_q0[5]), .d6(GND),
    .q6(shift_register_1_q0[6]), .d7(GND), .q7(shift_register_1_q0[7]));
  not not_1 (not_1_out, OE_prime);
  not not_2 (not_2_out, SRCLR_prime);
  Register register_1 (.D(shift_register_1_q0), .en(Vcc), .Q(register_1_q), .clk(RCLK), .clr(GND));
  not not_3 (Qh_prime, shift_register_1_out);
  // also tied to GND on the sheet: GND
  // also tied to VCC on the sheet: Vcc
endmodule

// LS161
module SN74LS161A (
  input  CLR_prime,
  input  Vcc,
  input  CLK,
  input  [3:0] D,
  input  ENP_prime,
  input  ENT_prime,
  input  GND,
  input  LOAD_prime,
  output RCO_prime,
  output [3:0] Q
);

  wire and_1_out, counter_1_carry, not_1_out, not_2_out, rising_edge_detector_1_out_2;

  not not_1 (not_1_out, LOAD_prime);
  not not_2 (not_2_out, CLR_prime);
  Rising_Edge_Detector rising_edge_detector_1 (.in_1(CLK), .out_2(rising_edge_detector_1_out_2));
  Counter #(.width(4), .max('hf)) counter_1 (
    .load(not_1_out), .D(D), .count(LOAD_prime), .Q(Q), .carry(counter_1_carry), .clk(and_1_out),
    .clr(not_2_out));
  and and_1 (and_1_out, ~ENP_prime, rising_edge_detector_1_out_2, ~ENT_prime);  // AND_Gate
  nand nand_1 (RCO_prime, ~ENT_prime, counter_1_carry);  // NAND_Gate
  // also tied to GND on the sheet: GND
  // also tied to VCC on the sheet: Vcc
endmodule

// LS163
module SN74LS169BN (
  input  U_D_prime,
  input  Vcc,
  input  CLK,
  input  [3:0] D,
  input  ENP_prime,
  input  ENT_prime,
  input  GND,
  input  LOAD_prime,
  output RCO_prime,
  output [3:0] Q
);

  wire and_1_out, and_2_out, controlled_buffer_2_out, controlled_inverter_1_out, counter_1_carry, not_1_out,
       not_2_out, or_1_out, rising_edge_detector_1_out_2;

  Pull_Resistor pull_resistor_1 (.node(U_D_prime));
  assign controlled_inverter_1_out = LOAD_prime ? ~U_D_prime : 1'bz;  // Controlled_Inverter controlled_inverter_1
  assign controlled_inverter_1_out = not_1_out ? not_1_out : 1'bz;  // Controlled_Buffer controlled_buffer_1
  not not_1 (not_1_out, LOAD_prime);
  assign controlled_buffer_2_out = LOAD_prime ? CLK : 1'bz;  // Controlled_Buffer controlled_buffer_2
  assign controlled_buffer_2_out = not_2_out ? LOAD_prime : 1'bz;  // Controlled_Buffer controlled_buffer_3
  not not_2 (not_2_out, LOAD_prime);
  Counter #(.width(4), .max('hf)) counter_1 (
    .load(controlled_inverter_1_out), .D(D), .count(controlled_buffer_2_out), .Q(Q), .carry(counter_1_carry),
    .clk(or_1_out), .clr(1'b0));
  or or_1 (or_1_out, and_1_out, and_2_out);
  and and_1 (and_1_out, ~ENP_prime, rising_edge_detector_1_out_2, ~ENT_prime);  // AND_Gate
  Rising_Edge_Detector rising_edge_detector_1 (.in_1(CLK), .out_2(rising_edge_detector_1_out_2));
  nand nand_1 (RCO_prime, ~ENT_prime, counter_1_carry);  // NAND_Gate
  and and_2 (and_2_out, rising_edge_detector_1_out_2, ~ENP_prime, ~LOAD_prime);  // AND_Gate
  // also tied to GND on the sheet: GND
  // also tied to VCC on the sheet: Vcc
endmodule

module Adder16 (
  input  [15:0] A,
  input  [15:0] B,
  input  CI,
  output [15:0] Q,
  output CO
);

  wire sn74f283n_1_co, sn74f283n_2_co, sn74f283n_3_co;

  SN74F283N sn74f283n_1 (
    .Q2(Q[1]), .B2(B[1]), .A2(A[1]), .Q1(Q[0]), .B1(B[0]), .A1(A[0]), .CI(CI), .B3(B[2]), .A3(A[2]),
    .Q3(Q[2]), .B4(B[3]), .A4(A[3]), .Q4(Q[3]), .CO(sn74f283n_1_co));  // open: GND, Vcc
  SN74F283N sn74f283n_2 (
    .Q2(Q[5]), .B2(B[5]), .A2(A[5]), .Q1(Q[4]), .B1(B[4]), .A1(A[4]), .CI(sn74f283n_1_co), .B3(B[6]),
    .A3(A[6]), .Q3(Q[6]), .B4(B[7]), .A4(A[7]), .Q4(Q[7]), .CO(sn74f283n_2_co));  // open: GND, Vcc
  SN74F283N sn74f283n_3 (
    .Q2(Q[9]), .B2(B[9]), .A2(A[9]), .Q1(Q[8]), .B1(B[8]), .A1(A[8]), .CI(sn74f283n_2_co), .B3(B[10]),
    .A3(A[10]), .Q3(Q[10]), .B4(B[11]), .A4(A[11]), .Q4(Q[11]), .CO(sn74f283n_3_co));  // open: GND, Vcc
  SN74F283N sn74f283n_4 (
    .Q2(Q[13]), .B2(B[13]), .A2(A[13]), .Q1(Q[12]), .B1(B[12]), .A1(A[12]), .CI(sn74f283n_3_co), .B3(B[14]),
    .A3(A[14]), .Q3(Q[14]), .B4(B[15]), .A4(A[15]), .Q4(Q[15]), .CO(CO));  // open: GND, Vcc
endmodule

module Counter8 (
  input  U_D_prime,
  input  CLK,
  input  LOAD_prime,
  input  [7:0] D,
  output CO_prime,
  output [7:0] Q
);

  wire sn74ls169bn_1_rco_prime;

  SN74LS169BN sn74ls169bn_1 (
    .U_D_prime(U_D_prime), .CLK(CLK), .D(D[3:0]), .ENP_prime(1'b0), .GND(1'b0), .Vcc(1'b1),
    .RCO_prime(sn74ls169bn_1_rco_prime), .Q(Q[3:0]), .ENT_prime(1'b0), .LOAD_prime(LOAD_prime));
  SN74LS169BN sn74ls169bn_2 (
    .U_D_prime(U_D_prime), .CLK(CLK), .D(D[7:4]), .ENP_prime(1'b0), .GND(1'b0), .Vcc(1'b1),
    .RCO_prime(CO_prime), .Q(Q[7:4]), .ENT_prime(sn74ls169bn_1_rco_prime), .LOAD_prime(LOAD_prime));
endmodule

module Counter16 (
  input  U_D_prime,
  input  CLK,
  input  CE_prime,
  input  LOAD_prime,
  input  [15:0] D,
  output CO_prime,
  output [15:0] Q
);

  wire sn74ls169bn_1_rco_prime, sn74ls169bn_2_rco_prime, sn74ls169bn_3_rco_prime;

  SN74LS169BN sn74ls169bn_1 (
    .U_D_prime(U_D_prime), .CLK(CLK), .D(D[3:0]), .ENP_prime(CE_prime), .GND(1'b0), .Vcc(1'b1),
    .RCO_prime(sn74ls169bn_1_rco_prime), .Q(Q[3:0]), .ENT_prime(1'b0), .LOAD_prime(LOAD_prime));
  SN74LS169BN sn74ls169bn_2 (
    .U_D_prime(U_D_prime), .CLK(CLK), .D(D[7:4]), .ENP_prime(CE_prime), .GND(1'b0), .Vcc(1'b1),
    .RCO_prime(sn74ls169bn_2_rco_prime), .Q(Q[7:4]), .ENT_prime(sn74ls169bn_1_rco_prime),
    .LOAD_prime(LOAD_prime));
  SN74LS169BN sn74ls169bn_3 (
    .U_D_prime(U_D_prime), .CLK(CLK), .D(D[11:8]), .ENP_prime(CE_prime), .GND(1'b0), .Vcc(1'b1),
    .RCO_prime(sn74ls169bn_3_rco_prime), .Q(Q[11:8]), .ENT_prime(sn74ls169bn_2_rco_prime),
    .LOAD_prime(LOAD_prime));
  SN74LS169BN sn74ls169bn_4 (
    .U_D_prime(U_D_prime), .CLK(CLK), .D(D[15:12]), .ENP_prime(CE_prime), .GND(1'b0), .Vcc(1'b1),
    .RCO_prime(CO_prime), .Q(Q[15:12]), .ENT_prime(sn74ls169bn_3_rco_prime), .LOAD_prime(LOAD_prime));
endmodule

module Register16 (
  input  OE,
  input  LE,
  input  [15:0] D,
  output [15:0] Q
);

  wire not_1_out, not_2_out;

  not not_1 (not_1_out, OE);
  not not_2 (not_2_out, LE);
  CD74HCT573E cd74hct573e_1 (
    .OE_prime(not_1_out), .D(D[7:0]), .GND(1'b0), .Vcc(1'b1), .Q(Q[7:0]), .LE_prime(not_2_out));
  CD74HCT573E cd74hct573e_2 (
    .OE_prime(not_1_out), .D(D[15:8]), .GND(1'b0), .Vcc(1'b1), .Q(Q[15:8]), .LE_prime(not_2_out));
endmodule

// CU
module Control_Unit (
  input  JF,
  input  JE,
  input  [15:0] Instruction,
  input  CLK,
  input  INT,
  input  IRD,
  output [31:0] CONTROL_WORD
);

  wire and_3_out, and_4_out, nand_1_out, not_1_out, not_2_out, not_3_out, not_4_out, or_1_out, or_4_out,
       or_5_out, rising_edge_detector_1_out_2;
  wire [2:1] rom_1_data;
  wire [3:0] and_1_out, and_2_out, cd4043be_1_q, sn74ls161a_1_q;
  wire [15:0] controlled_buffer_1_out;

  assign controlled_buffer_1_out = not_1_out ? Instruction : 16'bz;  // Controlled_Buffer controlled_buffer_1
  nand nand_1 (nand_1_out, rising_edge_detector_1_out_2, CONTROL_WORD[31]);
  Rising_Edge_Detector rising_edge_detector_1 (.in_1(CLK), .out_2(rising_edge_detector_1_out_2));
  not not_1 (not_1_out, cd4043be_1_q[0]);
  Floating_1 floating_1_1 (.D(cd4043be_1_q[0]), .Q(controlled_buffer_1_out[0]));
  Pull_Resistor pull_resistor_1 (.node(controlled_buffer_1_out));
  SN74LS161A sn74ls161a_1 (
    .CLR_prime(nand_1_out), .CLK(CLK), .ENP_prime(1'b0), .Q(sn74ls161a_1_q), .ENT_prime(1'b0),
    .LOAD_prime(1'b1));  // open: D, GND, Vcc, RCO_prime
  CD4043BE cd4043be_1 (.S(and_2_out), .R(and_1_out), .Q(cd4043be_1_q), .E(1'b1));
  and and_1 (and_1_out[0], rising_edge_detector_1_out_2, CONTROL_WORD[31]);
  and and_2 (and_2_out[0], and_3_out, not_3_out);
  not not_2 (not_2_out, JF);
  ROM #(.addrWidth(20), .dataWidth(32)) rom_1 (
    .addr({controlled_buffer_1_out, sn74ls161a_1_q}),
    .data({CONTROL_WORD[31:3], rom_1_data, CONTROL_WORD[0]}), .sel(1'b1));
  and and_3 (and_3_out, not_4_out, INT);
  not not_3 (not_3_out, IRD);
  and and_4 (and_4_out, JE, not_2_out);
  or or_1 (or_1_out, or_4_out, or_5_out);
  not not_4 (not_4_out, or_1_out);
  or or_2 (CONTROL_WORD[1], and_4_out, rom_1_data[1]);
  or or_3 (CONTROL_WORD[2], JF, rom_1_data[2]);
  or or_4 (or_4_out, sn74ls161a_1_q[0], sn74ls161a_1_q[1]);
  or or_5 (or_5_out, sn74ls161a_1_q[2], sn74ls161a_1_q[3]);
  Pull_Resistor pull_resistor_2 (.node(INT));

  // Notes on the sheet:
  //   Instruction: pull=down
  //   CONTROL_WORD: pull=down
  //   contents of rom_1 (hex, n*v repeats v):
  //   400044 15*80000000 42674000 22 43400000 22 27c014 42c00000 22 3c0000c 80400044 7*80000000 400044
  //   2400014 20 240000c 20 246c000 20 8000000a 8*80000000 400044 8000000a 14*80000000 400044 a 484000 a
  //   402f80 41601f80 8000000a 9*80000000 400044 a 504000 a 484000 a 402f80 41e01f80 8000000a 7*80000000
  //   400044 42674000 22 8000000a 12*80000000 400044 20 246c000 8000000a 12*80000000 400044 a 42c84000
  //   160000c 12*80000000 400044 4350400a 42c84000 1e00014 a 42c84000 160000c 9*80000000 400044 4350400a
  //   22 42c84000 160000c 80000022 10*80000000 400044 4350400a 22 42c84000 1e00014 a 42c84000 160000c
  //   80000022 7*80000000 400044 20 240000c 20 2400014 8000000a 10*80000000 400044 43400000 8000002a
  //   13*80000000 400044 22 2400014 8000000a 12*80000000 400044 a 484000 42634000 8000002a 11*80000000
  //   400044 a 402080 8000000a 12*80000000 400044 a 402180 8000000a 12*80000000 400044 a 402280 8000000a
  //   12*80000000 400044 a 402380 8000000a 12*80000000 400044 a 402480 8000000a 12*80000000 400044 a
  //   402580 8000000a 12*80000000 400044 a 402680 8000000a 12*80000000 400044 a 402780 8000000a
  //   12*80000000 400044 a 402880 8000000a 12*80000000 400044 a 402980 8000000a 12*80000000 400044 a
  //   402a80 8000000a 12*80000000 400044 a 402b80 8000000a 12*80000000 400044 a 402c80 8000000a
  //   12*80000000 400044 a 402d80 8000000a 12*80000000 400044 a 402e80 8000000a 12*80000000 400044 a
  //   402f80 8000000a 12*80000000 400044 a 484000 402080 8000000a 11*80000000 400044 a 484000 402180
  //   8000000a 11*80000000 400044 a 484000 402280 8000000a 11*80000000 400044 a 484000 402380 8000000a
  //   11*80000000 400044 a 484000 402480 8000000a 11*80000000 400044 a 484000 402580 8000000a 11*80000000
  //   400044 a 484000 402680 8000000a 11*80000000 400044 a 484000 402780 8000000a 11*80000000 400044 a
  //   484000 402880 8000000a 11*80000000 400044 a 484000 402980 8000000a 11*80000000 400044 a 484000
  //   402a80 8000000a 11*80000000 400044 a 484000 402b80 8000000a 11*80000000 400044 a 484000 402c80
  //   8000000a 11*80000000 400044 a 484000 402d80 8000000a 11*80000000 400044 a 484000 402e80 8000000a
  //   11*80000000 400044 a 484000 402f80 8000000a 11*80000000 400044 a 484000 a 504000 1e02080 8000000a
  //   9*80000000 400044 a 484000 a 504000 1e02180 8000000a 9*80000000 400044 a 484000 a 504000 1e02280
  //   8000000a 9*80000000 400044 a 484000 a 504000 1e02380 8000000a 9*80000000 400044 a 484000 a 504000
  //   1e02480 8000000a 9*80000000 400044 a 484000 a 504000 1e02580 8000000a 9*80000000 400044 a 484000 a
  //   504000 1e02680 8000000a 9*80000000 400044 a 484000 a 504000 1e02780 8000000a 9*80000000 400044 a
  //   484000 a 504000 1e02880 8000000a 9*80000000 400044 a 484000 a 504000 1e02980 8000000a 9*80000000
  //   400044 a 484000 a 504000 1e02a80 8000000a 9*80000000 400044 a 484000 a 504000 1e02b80 8000000a
  //   9*80000000 400044 a 484000 a 504000 1e02c80 8000000a 9*80000000 400044 a 484000 a 504000 1e02d80
  //   8000000a 9*80000000 400044 a 484000 a 504000 1e02e80 8000000a 9*80000000 400044 a 484000 a 504000
  //   1e02f80 8000000a 9*80000000 400044 a 484000 41601080 8000000a 11*80000000 400044 a 484000 41601180
  //   8000000a 11*80000000 400044 a 484000 41601280 8000000a 11*80000000 400044 a 484000 41601380 8000000a
  //   11*80000000 400044 a 484000 41601480 8000000a 11*80000000 400044 a 484000 41601580 8000000a
  //   11*80000000 400044 a 484000 41601680 8000000a 11*80000000 400044 a 484000 41601780 8000000a
  //   11*80000000 400044 a 484000 41601880 8000000a 11*80000000 400044 a 484000 41601980 8000000a
  //   11*80000000 400044 a 484000 41601a80 8000000a 11*80000000 400044 a 484000 41601b80 8000000a
  //   11*80000000 400044 a 484000 41601c80 8000000a 11*80000000 400044 a 484000 41601d80 8000000a
  //   11*80000000 400044 a 484000 41601e80 8000000a 11*80000000 400044 a 484000 41601f80 8000000a
  //   11*80000000 400044 a 484000 a 504000 41e01080 8000000a 9*80000000 400044 a 484000 a 504000 41e01180
  //   8000000a 9*80000000 400044 a 484000 a 504000 41e01280 8000000a 9*80000000 400044 a 484000 a 504000
  //   41e01380 8000000a 9*80000000 400044 a 484000 a 504000 41e01480 8000000a 9*80000000 400044 a 484000 a
  //   504000 41e01580 8000000a 9*80000000 400044 a 484000 a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
endmodule

// FLG
module Flag_Unit (
  input  [15:0] D,
  input  SEC,
  input  CLC,
  input  FE_prime,
  input  SUF,
  output [7:0] F
);

  wire not_4_out, not_6_out, or_1_out, or_2_out, or_3_out, or_4_out, or_5_out, or_6_out, or_7_out, or_8_out,
       or_9_out, or_10_out, or_11_out, or_12_out, or_13_out, or_14_out;
  wire [1:1] not_3_out;
  wire [3:0] controlled_buffer_1_out, controlled_buffer_2_out, not_5_out;
  wire [3:1] or_15_out;

  not not_1 (or_15_out[2], D[0]);
  not not_2 (or_15_out[3], D[15]);
  not not_3 (not_3_out[1], or_15_out[1]);
  assign controlled_buffer_1_out = not_4_out ? {D[15], D[0], not_3_out[1], SEC} : 4'bz;  // Controlled_Buffer controlled_buffer_1
  assign controlled_buffer_2_out = SUF ? not_5_out : 4'bz;  // Controlled_Buffer controlled_buffer_2
  assign controlled_buffer_2_out = not_4_out ? {or_15_out, CLC} : 4'bz;  // Controlled_Buffer controlled_buffer_3
  assign controlled_buffer_1_out = SUF ? D[3:0] : 4'bz;  // Controlled_Buffer controlled_buffer_4
  not not_4 (not_4_out, SUF);
  assign not_5_out = ~D[3:0];  // NOT_Gate not_5, 4 bits wide
  or or_1 (or_1_out, D[0], D[1]);
  or or_2 (or_2_out, D[2], D[3]);
  or or_3 (or_3_out, D[4], D[5]);
  or or_4 (or_4_out, D[6], D[7]);
  or or_5 (or_5_out, D[8], D[9]);
  or or_6 (or_6_out, D[10], D[11]);
  or or_7 (or_7_out, D[12], D[13]);
  or or_8 (or_8_out, D[14], D[15]);
  CD4043BE cd4043be_1 (.S(controlled_buffer_1_out), .R(controlled_buffer_2_out), .Q(F[3:0]), .E(not_6_out));
  CD4043BE cd4043be_2 (.S(D[3:0]), .R(not_5_out), .Q(F[7:4]), .E(SUF));
  or or_9 (or_9_out, or_1_out, or_2_out);
  or or_10 (or_10_out, or_3_out, or_4_out);
  or or_11 (or_11_out, or_5_out, or_6_out);
  or or_12 (or_12_out, or_7_out, or_8_out);
  or or_13 (or_13_out, or_9_out, or_10_out);
  or or_14 (or_14_out, or_11_out, or_12_out);
  not not_6 (not_6_out, FE_prime);
  or or_15 (or_15_out[1], or_13_out, or_14_out);

  // Notes on the sheet:
  //   Flags A-D can only be set when the SUF line is high, which will also cause the S, P, Z and F flags to be loaded from the low bye of D
  //   D
  //   A
  //   C
  //   Z
  //   S
  //   B
  //   P
  //   V
endmodule

// GPR
module General_Purpose_Registers (
  input  EN,
  input  [3:0] RS,
  input  OE,
  input  LE,
  input  [15:0] D,
  output [15:0] Q,
  output [15:0] F
);

  wire and_1_out, and_2_out, and_3_out, and_4_out, and_5_out, nand_1_out, nand_2_out, nand_3_out, nand_4_out,
       nand_5_out, nand_6_out, nand_7_out, nand_8_out, not_1_out, not_2_out, not_3_out, not_4_out;

  nand nand_1 (nand_1_out, OE, and_2_out);
  nand nand_2 (nand_2_out, and_1_out, and_2_out);
  nand nand_3 (nand_3_out, OE, and_3_out);
  nand nand_4 (nand_4_out, and_1_out, and_3_out);
  and and_1 (and_1_out, EN, LE);
  nand nand_5 (nand_5_out, OE, and_4_out);
  nand nand_6 (nand_6_out, and_1_out, and_4_out);
  and and_2 (and_2_out, RS[2], RS[3]);
  and and_3 (and_3_out, not_1_out, RS[3]);
  not not_1 (not_1_out, RS[2]);
  nand nand_7 (nand_7_out, OE, and_5_out);
  nand nand_8 (nand_8_out, and_1_out, and_5_out);
  and and_4 (and_4_out, RS[2], not_2_out);
  and and_5 (and_5_out, not_3_out, not_4_out);
  not not_2 (not_2_out, RS[3]);
  not not_3 (not_3_out, RS[2]);
  not not_4 (not_4_out, RS[3]);
  CD74HC670E cd74hc670e_1 (
    .D(D[15:12]), .RA1(RS[1]), .RA0(RS[0]), .WA0(RS[0]), .WA1(RS[1]), .WE_prime(nand_2_out),
    .RE_prime(nand_1_out), .Q(Q[15:12]));  // open: F
  CD74HC670E cd74hc670e_2 (
    .D(D[15:12]), .RA1(RS[1]), .RA0(RS[0]), .WA0(RS[0]), .WA1(RS[1]), .WE_prime(nand_4_out),
    .RE_prime(nand_3_out), .Q(Q[15:12]));  // open: F
  CD74HC670E cd74hc670e_3 (
    .D(D[15:12]), .RA1(RS[1]), .RA0(RS[0]), .WA0(RS[0]), .WA1(RS[1]), .WE_prime(nand_6_out),
    .RE_prime(nand_5_out), .Q(Q[15:12]));  // open: F
  CD74HC670E cd74hc670e_4 (
    .D(D[15:12]), .RA1(RS[1]), .RA0(RS[0]), .F(F[15:12]), .WA0(RS[0]), .WA1(RS[1]), .WE_prime(nand_8_out),
    .RE_prime(nand_7_out), .Q(Q[15:12]));
  CD74HC670E cd74hc670e_5 (
    .D(D[11:8]), .RA1(RS[1]), .RA0(RS[0]), .WA0(RS[0]), .WA1(RS[1]), .WE_prime(nand_2_out),
    .RE_prime(nand_1_out), .Q(Q[11:8]));  // open: F
  CD74HC670E cd74hc670e_6 (
    .D(D[11:8]), .RA1(RS[1]), .RA0(RS[0]), .WA0(RS[0]), .WA1(RS[1]), .WE_prime(nand_4_out),
    .RE_prime(nand_3_out), .Q(Q[11:8]));  // open: F
  CD74HC670E cd74hc670e_7 (
    .D(D[11:8]), .RA1(RS[1]), .RA0(RS[0]), .WA0(RS[0]), .WA1(RS[1]), .WE_prime(nand_6_out),
    .RE_prime(nand_5_out), .Q(Q[11:8]));  // open: F
  CD74HC670E cd74hc670e_8 (
    .D(D[11:8]), .RA1(RS[1]), .RA0(RS[0]), .F(F[11:8]), .WA0(RS[0]), .WA1(RS[1]), .WE_prime(nand_8_out),
    .RE_prime(nand_7_out), .Q(Q[11:8]));
  CD74HC670E cd74hc670e_9 (
    .D(D[7:4]), .RA1(RS[1]), .RA0(RS[0]), .WA0(RS[0]), .WA1(RS[1]), .WE_prime(nand_2_out),
    .RE_prime(nand_1_out), .Q(Q[7:4]));  // open: F
  CD74HC670E cd74hc670e_10 (
    .D(D[7:4]), .RA1(RS[1]), .RA0(RS[0]), .WA0(RS[0]), .WA1(RS[1]), .WE_prime(nand_4_out),
    .RE_prime(nand_3_out), .Q(Q[7:4]));  // open: F
  CD74HC670E cd74hc670e_11 (
    .D(D[7:4]), .RA1(RS[1]), .RA0(RS[0]), .WA0(RS[0]), .WA1(RS[1]), .WE_prime(nand_6_out),
    .RE_prime(nand_5_out), .Q(Q[7:4]));  // open: F
  CD74HC670E cd74hc670e_12 (
    .D(D[7:4]), .RA1(RS[1]), .RA0(RS[0]), .F(F[7:4]), .WA0(RS[0]), .WA1(RS[1]), .WE_prime(nand_8_out),
    .RE_prime(nand_7_out), .Q(Q[7:4]));
  CD74HC670E cd74hc670e_13 (
    .D(D[3:0]), .RA1(RS[1]), .RA0(RS[0]), .WA0(RS[0]), .WA1(RS[1]), .WE_prime(nand_2_out),
    .RE_prime(nand_1_out), .Q(Q[3:0]));  // open: F
  CD74HC670E cd74hc670e_14 (
    .D(D[3:0]), .RA1(RS[1]), .RA0(RS[0]), .WA0(RS[0]), .WA1(RS[1]), .WE_prime(nand_4_out),
    .RE_prime(nand_3_out), .Q(Q[3:0]));  // open: F
  CD74HC670E cd74hc670e_15 (
    .D(D[3:0]), .RA1(RS[1]), .RA0(RS[0]), .WA0(RS[0]), .WA1(RS[1]), .WE_prime(nand_6_out),
    .RE_prime(nand_5_out), .Q(Q[3:0]));  // open: F
  CD74HC670E cd74hc670e_16 (
    .D(D[3:0]), .RA1(RS[1]), .RA0(RS[0]), .F(F[3:0]), .WA0(RS[0]), .WA1(RS[1]), .WE_prime(nand_8_out),
    .RE_prime(nand_7_out), .Q(Q[3:0]));
endmodule

// ALU
module alu (
  input  [15:0] D,
  input  OE,
  input  LEA,
  input  JF,
  input  LEB,
  input  EN,
  input  [3:0] OP,
  input  A32,
  input  A16,
  output [15:0] Q,
  output [31:0] A,
  output [7:0] FLAGS
);

  wire a___b_2_co, a___b_co, and_1_out, and_2_out, dec_a_co, decoder_1_out0, decoder_1_out1, decoder_1_out2,
       decoder_1_out3, decoder_1_out4, decoder_1_out5, decoder_1_out6, decoder_1_out7, decoder_1_out8,
       decoder_1_out9, decoder_1_out10, decoder_1_out11, decoder_1_out12, decoder_1_out13, decoder_1_out14,
       decoder_1_out15, flag_selector_1_q, flag_selector_1_q_prime, inc_a_co;
  wire [15:0] a___b_2_q, a___b_q, A_q, and_3_out, B_q, controlled_buffer_1_out, dec_a_q, inc_a_q, not_1_out,
       or_1_out, xor_1_out;

  and and_1 (and_1_out, LEA, EN);
  and and_2 (and_2_out, LEB, EN);
  Register16 u_A (.OE(OE), .LE(and_1_out), .D(D), .Q(A_q));
  Register16 B (.OE(OE), .LE(and_2_out), .D(D), .Q(B_q));
  Adder16 a___b (.A(A_q), .B(B_q), .Q(a___b_q), .CO(a___b_co));  // open: CI
  Adder16 a___b_2 (.A(A_q), .B(not_1_out), .CI(1'b1), .Q(a___b_2_q), .CO(a___b_2_co));
  assign not_1_out = ~B_q;  // NOT_Gate not_1, 16 bits wide
  assign and_3_out = A_q & B_q;  // AND_Gate and_3, 16 bits wide
  assign or_1_out = A_q | B_q;  // OR_Gate or_1, 16 bits wide
  assign xor_1_out = A_q ^ B_q;  // XOR_Gate xor_1, 16 bits wide
  Adder16 inc_a (.A(A_q), .B({16{1'b0}}), .CI(1'b1), .Q(inc_a_q), .CO(inc_a_co));
  Adder16 dec_a (.A(A_q), .B({16{1'b1}}), .Q(dec_a_q), .CO(dec_a_co));  // open: CI
  assign controlled_buffer_1_out = decoder_1_out0 ? a___b_q : 16'bz;  // Controlled_Buffer controlled_buffer_1
  Flag_Selector flag_selector_1 (
    .F(a___b_co), .Q(flag_selector_1_q), .Q_prime(flag_selector_1_q_prime), .E(decoder_1_out0));
  assign controlled_buffer_1_out = decoder_1_out1 ? a___b_2_q : 16'bz;  // Controlled_Buffer controlled_buffer_2
  assign controlled_buffer_1_out = decoder_1_out2 ? ~A_q : 16'bz;  // Controlled_Inverter controlled_inverter_1
  assign controlled_buffer_1_out = decoder_1_out3 ? and_3_out : 16'bz;  // Controlled_Buffer controlled_buffer_3
  assign controlled_buffer_1_out = decoder_1_out4 ? or_1_out : 16'bz;  // Controlled_Buffer controlled_buffer_4
  assign controlled_buffer_1_out = decoder_1_out5 ? xor_1_out : 16'bz;  // Controlled_Buffer controlled_buffer_5
  Decoder #(.select(4), .disabled(0)) decoder_1 (
    .out0(decoder_1_out0), .out1(decoder_1_out1), .out2(decoder_1_out2), .out3(decoder_1_out3),
    .out4(decoder_1_out4), .out5(decoder_1_out5), .out6(decoder_1_out6), .out7(decoder_1_out7),
    .out8(decoder_1_out8), .out9(decoder_1_out9), .out10(decoder_1_out10), .out11(decoder_1_out11),
    .out12(decoder_1_out12), .out13(decoder_1_out13), .out14(decoder_1_out14), .out15(decoder_1_out15),
    .sel(OP), .en(EN));
  Flag_Selector flag_selector_2 (
    .F(a___b_2_co), .Q(flag_selector_1_q), .Q_prime(flag_selector_1_q_prime), .E(decoder_1_out1));
  assign controlled_buffer_1_out = decoder_1_out6 ? A_q : 16'bz;  // Controlled_Buffer controlled_buffer_6
  assign controlled_buffer_1_out = decoder_1_out7 ? {A_q[14:0], 1'b0} : 16'bz;  // Controlled_Buffer controlled_buffer_7
  assign controlled_buffer_1_out = decoder_1_out8 ? {1'b0, A_q[15:1]} : 16'bz;  // Controlled_Buffer controlled_buffer_8
  assign controlled_buffer_1_out = decoder_1_out9 ? {A_q[14:0], A_q[15]} : 16'bz;  // Controlled_Buffer controlled_buffer_9
  assign controlled_buffer_1_out = decoder_1_out10 ? {A_q[0], A_q[15:1]} : 16'bz;  // Controlled_Buffer controlled_buffer_10
  assign controlled_buffer_1_out = decoder_1_out12 ? dec_a_q : 16'bz;  // Controlled_Buffer controlled_buffer_11
  Flag_Selector flag_selector_3 (.F(A_q[15]), .Q(flag_selector_1_q), .Q_prime(flag_selector_1_q), .E(decoder_1_out7));
  assign controlled_buffer_1_out = decoder_1_out11 ? inc_a_q : 16'bz;  // Controlled_Buffer controlled_buffer_12
  Flag_Selector flag_selector_4 (
    .F(inc_a_co), .Q(flag_selector_1_q), .Q_prime(flag_selector_1_q_prime), .E(decoder_1_out11));
  Flag_Selector flag_selector_5 (
    .F(dec_a_co), .Q(flag_selector_1_q), .Q_prime(flag_selector_1_q_prime), .E(decoder_1_out12));
  assign A = A32 ? {B_q, A_q} : 32'bz;  // Controlled_Buffer controlled_buffer_13
  assign A[15:0] = A16 ? A_q : 16'bz;  // Controlled_Buffer controlled_buffer_14
  assign controlled_buffer_1_out = decoder_1_out13 ? D : 16'bz;  // Controlled_Buffer controlled_buffer_15
  assign controlled_buffer_1_out = decoder_1_out15 ? {16{1'b0}} : 16'bz;  // Controlled_Buffer controlled_buffer_16
  assign Q = OE ? controlled_buffer_1_out : 16'bz;  // Controlled_Buffer controlled_buffer_17
  Pull_Resistor pull_resistor_1 (.node(flag_selector_1_q));
  Pull_Resistor pull_resistor_2 (.node(flag_selector_1_q_prime));
  assign controlled_buffer_1_out[7:0] = decoder_1_out14 ? FLAGS : 8'bz;  // Controlled_Buffer controlled_buffer_18
  Flag_Unit flag_unit_1 (
    .D(controlled_buffer_1_out), .SEC(flag_selector_1_q), .CLC(flag_selector_1_q_prime),
    .SUF(decoder_1_out13), .F(FLAGS), .FE_prime(JF));

  // Notes on the sheet:
  //   a << 1
  //   a >> 1
  //   rol a
  //   ror a
  //   a and b
  //   a or b
  //   a xor b
  //   not a
  //   test a
endmodule

// CPU
module cpu (
  input  [15:0] D,
  input  [3:0] IRQ,
  input  INT,
  output R_prime_W,
  output CLK,
  output [15:0] Q,
  output [31:0] A
);

  wire and_1_out, and_2_out, and_3_out, counter16_1_co_prime, counter16_2_co_prime, counter16_3_co_prime,
       mmu_1_a16, mmu_1_a32, multiplexer_1_out, nor_1_out, not_1_out, not_2_out, not_3_out, not_4_out,
       not_5_out, not_6_out, not_7_out, or_1_out;
  wire [7:0] alu_1_flags;
  wire [15:0] counter16_1_q, counter16_2_q, counter16_3_q, counter16_4_q, general_purpose_registers_1_f;
  wire [31:0] pull_resistor_1_node;

  Clock clock_1 (.out(CLK));
  not not_1 (not_1_out, pull_resistor_1_node[2]);
  Pull_Resistor pull_resistor_1 (.node({pull_resistor_1_node[31], R_prime_W, pull_resistor_1_node[29:0]}));
  not not_2 (not_2_out, pull_resistor_1_node[3]);
  Counter16 counter16_1 (
    .U_D_prime(pull_resistor_1_node[1]), .CLK(CLK), .CE_prime(not_2_out), .LOAD_prime(not_1_out), .D(D),
    .CO_prime(counter16_1_co_prime), .Q(counter16_1_q));
  nor nor_1 (nor_1_out, ~counter16_1_co_prime, pull_resistor_1_node[4]);  // NOR_Gate
  Counter16 counter16_2 (
    .U_D_prime(pull_resistor_1_node[1]), .CLK(CLK), .CE_prime(nor_1_out),
    .LOAD_prime(pull_resistor_1_node[2]), .D(D), .CO_prime(counter16_2_co_prime), .Q(counter16_2_q));
  not not_3 (not_3_out, pull_resistor_1_node[5]);
  not not_4 (not_4_out, pull_resistor_1_node[2]);
  Counter16 counter16_3 (
    .U_D_prime(pull_resistor_1_node[1]), .CLK(CLK), .CE_prime(not_3_out), .LOAD_prime(not_4_out), .D(D),
    .CO_prime(counter16_3_co_prime), .Q(counter16_3_q));
  mmu mmu_1 (
    .PC(counter16_1_q), .PR(counter16_2_q), .Stack(counter16_3_q), .F(general_purpose_registers_1_f),
    .IRQ(IRQ), .A16(mmu_1_a16), .A32(mmu_1_a32), .Q(D), .Addr(A), .EN(pull_resistor_1_node[22]),
    .in_7(pull_resistor_1_node[25:23]));
  not not_5 (not_5_out, pull_resistor_1_node[6]);
  not not_6 (not_6_out, pull_resistor_1_node[2]);
  not not_7 (not_7_out, CLK);
  Counter16 counter16_4 (
    .CLK(CLK), .CE_prime(not_5_out), .LOAD_prime(not_6_out), .D(D), .Q(counter16_4_q));  // open: U_D_prime, CO_prime
  Control_Unit control_unit_1 (
    .Instruction(counter16_4_q), .CLK(not_7_out), .JF(or_1_out), .JE(pull_resistor_1_node[26]),
    .IRD(alu_1_flags[3]), .CONTROL_WORD({pull_resistor_1_node[31], R_prime_W, pull_resistor_1_node[29:0]}),
    .INT(INT));
  and and_1 (and_1_out, pull_resistor_1_node[7], CLK);
  General_Purpose_Registers general_purpose_registers_1 (
    .EN(and_1_out), .RS(pull_resistor_1_node[11:8]), .OE(pull_resistor_1_node[12]),
    .LE(pull_resistor_1_node[13]), .D(D), .Q(D), .F(general_purpose_registers_1_f));
  DotMatrix #(.matrixcols(32), .matrixrows(1)) dotmatrix_1 (
    .col0(A[31]), .col1(A[30]), .col2(A[29]), .col3(A[28]), .col4(A[27]), .col5(A[26]), .col6(A[25]),
    .col7(A[24]), .col8(A[23]), .col9(A[22]), .col10(A[21]), .col11(A[20]), .col12(A[19]), .col13(A[18]),
    .col14(A[17]), .col15(A[16]), .col16(A[15]), .col17(A[14]), .col18(A[13]), .col19(A[12]), .col20(A[11]),
    .col21(A[10]), .col22(A[9]), .col23(A[8]), .col24(A[7]), .col25(A[6]), .col26(A[5]), .col27(A[4]),
    .col28(A[3]), .col29(A[2]), .col30(A[1]), .col31(A[0]));
  or or_1 (or_1_out, and_2_out, and_3_out);
  alu alu_1 (
    .D(D), .OE(pull_resistor_1_node[21]), .LEA(pull_resistor_1_node[19]), .LEB(pull_resistor_1_node[20]),
    .EN(pull_resistor_1_node[14]), .OP(pull_resistor_1_node[18:15]), .A(A), .A32(mmu_1_a32), .A16(mmu_1_a16),
    .Q(D), .FLAGS(alu_1_flags), .JF(multiplexer_1_out));
  Multiplexer #(.select(3), .disabled(0)) multiplexer_1 (
    .in0(alu_1_flags[7]), .in1(alu_1_flags[6]), .in2(alu_1_flags[5]), .in3(alu_1_flags[4]),
    .in4(alu_1_flags[3]), .in5(alu_1_flags[2]), .in6(alu_1_flags[1]), .in7(alu_1_flags[0]),
    .out(multiplexer_1_out), .sel(pull_resistor_1_node[29:27]), .en(pull_resistor_1_node[26]));
  and and_2 (and_2_out, ~multiplexer_1_out, pull_resistor_1_node[0]);  // AND_Gate
  and and_3 (and_3_out, multiplexer_1_out, ~pull_resistor_1_node[0]);  // AND_Gate
  DotMatrix #(.matrixcols(16), .matrixrows(1)) dotmatrix_2 (
    .col0(D[15]), .col1(D[14]), .col2(D[13]), .col3(D[12]), .col4(D[11]), .col5(D[10]), .col6(D[9]),
    .col7(D[8]), .col8(D[7]), .col9(D[6]), .col10(D[5]), .col11(D[4]), .col12(D[3]), .col13(D[2]),
    .col14(D[1]), .col15(D[0]));

  assign Q = D;

  // Notes on the sheet:
  //   PC
  //   PR
  //   SP
  //   PAGE OVERFLOW
  //   IR
  //   STACK OVERFLOW
  //   JNF
  //   CUD
  //   CLD
  //   PCE
  //   PRE
  //   SPE
  //   IRE
  //   REN
  //   RS0
  //   RS1
  //   RS2
  //   RS3
  //   ROE
  //   RLE
  //   AEN
  //   AI0
  //   AI1
  //   AI2
  //   AI3
  //   ALA
  //   ALB
  //   AOE
  //   MEN
  //   MS0
  //   MS1
  //   MS2
  //   JFE
  //   FS0
  //   FS1
  //   FS2
  //   MCR
endmodule

// MMU
module mmu (
  input  [3:0] IRQ,
  input  [15:0] PC,
  input  [15:0] PR,
  input  [15:0] Stack,
  input  [15:0] F,
  input  EN,
  input  [2:0] in_7,
  output A16,
  output A32,
  output [31:0] Addr,
  output [15:0] Q
);

  wire decoder_1_out0, decoder_1_out1, decoder_1_out4, decoder_1_out5, decoder_1_out6, decoder_1_out7,
       or_1_out, or_2_out, or_3_out;

  assign Addr[15:0] = decoder_1_out0 ? PC : 16'bz;  // Controlled_Buffer controlled_buffer_1
  assign Q = decoder_1_out5 ? PC : 16'bz;  // Controlled_Buffer controlled_buffer_2
  assign Addr[31:16] = or_1_out ? PR : 16'bz;  // Controlled_Buffer controlled_buffer_3
  assign Q = decoder_1_out6 ? PR : 16'bz;  // Controlled_Buffer controlled_buffer_4
  assign Addr[15:0] = or_2_out ? Stack : 16'bz;  // Controlled_Buffer controlled_buffer_5
  assign Addr[31:16] = or_2_out ? {16{1'b1}} : 16'bz;  // Controlled_Buffer controlled_buffer_6
  assign Addr[15:0] = decoder_1_out1 ? F : 16'bz;  // Controlled_Buffer controlled_buffer_7
  assign Addr = decoder_1_out7 ? {28'hfff, IRQ} : 32'bz;  // Controlled_Buffer controlled_buffer_8
  or or_1 (or_1_out, decoder_1_out0, decoder_1_out1);
  Decoder #(.select(3), .disabled(0)) decoder_1 (
    .out0(decoder_1_out0), .out1(decoder_1_out1), .out2(A16), .out3(A32), .out4(decoder_1_out4),
    .out5(decoder_1_out5), .out6(decoder_1_out6), .out7(decoder_1_out7), .sel(in_7), .en(EN));
  or or_2 (or_2_out, decoder_1_out4, or_3_out);
  or or_3 (or_3_out, decoder_1_out6, decoder_1_out5);
endmodule

module main (
  input  INT
);

  wire and_1_out, and_2_out, and_3_out, and_4_out, buffer_1_out, buffer_2_out, cpu_1_clk, cpu_1_r_prime_w,
       not_1_out, not_2_out, not_3_out, not_4_out, xnor_1_out;
  wire [15:0] controlled_buffer_1_out, controlled_buffer_2_out, cpu_1_q, pull_resistor_3_node, ram_1_data,
       rom_1_data;
  wire [31:0] cpu_1_a;

  buf buffer_1 (buffer_1_out, cpu_1_a[31]);
  buf buffer_2 (buffer_2_out, cpu_1_a[31]);
  Pull_Resistor #(.pull(1)) pull_resistor_1 (.node(buffer_1_out));
  Pull_Resistor pull_resistor_2 (.node(buffer_2_out));
  xnor xnor_1 (xnor_1_out, buffer_2_out, buffer_1_out);
  not not_1 (not_1_out, not_2_out);
  cpu cpu_1 (
    .R_prime_W(cpu_1_r_prime_w), .A(cpu_1_a), .CLK(cpu_1_clk), .D(controlled_buffer_2_out), .Q(cpu_1_q),
    .INT(INT));  // open: IRQ
  not not_2 (not_2_out, cpu_1_a[31]);
  and and_1 (and_1_out, not_2_out, xnor_1_out);
  and and_2 (and_2_out, not_1_out, xnor_1_out);
  assign controlled_buffer_1_out = cpu_1_r_prime_w ? cpu_1_q : 16'bz;  // Controlled_Buffer controlled_buffer_1
  not not_3 (not_3_out, cpu_1_r_prime_w);
  assign controlled_buffer_2_out = not_3_out ? controlled_buffer_1_out : 16'bz;  // Controlled_Buffer controlled_buffer_2
  ROM #(.addrWidth(16), .dataWidth(16)) rom_1 (.addr(cpu_1_a[15:0]), .data(rom_1_data), .sel(and_1_out));
  RAM #(.addrWidth(16), .dataWidth(16), .bus("separate")) ram_1 (
    .addr(cpu_1_a[15:0]), .din(pull_resistor_3_node), .data(ram_1_data), .str(cpu_1_r_prime_w),
    .sel(and_2_out), .clk(cpu_1_clk), .ld(not_4_out), .clr(1'b0));
  not not_4 (not_4_out, cpu_1_r_prime_w);
  Pull_Resistor pull_resistor_3 (.node(pull_resistor_3_node));
  assign controlled_buffer_1_out = and_1_out ? rom_1_data : 16'bz;  // Controlled_Buffer controlled_buffer_3
  and and_3 (and_3_out, and_2_out, cpu_1_r_prime_w);
  and and_4 (and_4_out, and_2_out, ~cpu_1_r_prime_w);  // AND_Gate
  assign controlled_buffer_1_out = and_4_out ? ram_1_data : 16'bz;  // Controlled_Buffer controlled_buffer_4
  assign pull_resistor_3_node = and_3_out ? controlled_buffer_1_out : 16'bz;  // Controlled_Buffer controlled_buffer_5

  // Notes on the sheet:
  //   contents of rom_1 (hex, n*v repeats v):
  //   8 b a 5 0 6 10 ffff 110 7 c 9 0 2 65506*0 16*e
endmodule
