// Logisim project alu.circ as structural Verilog: 10 circuits, main circuit main
module main (
  input  [15:0] IN,
  input  CLK,
  input  R_prime_W,
  input  RES_prime,
  input  F,
  input  A,
  input  B,
  input  EN,
  input  [3:0] OP,
  output [15:0] OUT,
  output [7:0] FLAGS
);

  wire A_msb, ADD_co, B_lsb, decoder_1_out0, decoder_1_out1, decoder_1_out2, decoder_1_out3, decoder_1_out4,
       decoder_1_out5, decoder_1_out6, decoder_1_out7, or_2_out, SUB_co;
  wire [7:0] pull_resistor_3_node;
  wire [15:0] A_out, ADD_out, AND_out, B_out, controlled_buffer_1_out, not_1_out, OR_out, SUB_out, XOR_out;

  Decoder #(.select(4), .disabled(0)) decoder_1 (
    .out0(decoder_1_out0), .out1(decoder_1_out1), .out2(decoder_1_out2), .out3(decoder_1_out3),
    .out4(decoder_1_out4), .out5(decoder_1_out5), .out6(decoder_1_out6), .out7(decoder_1_out7), .sel(OP),
    .en(EN));  // open: out8, out9, out10, out11, out12, out13, out14, out15
  shift_register16 u_A (
    .IN(IN), .SHIFT(decoder_1_out6), .CLK(CLK), .R_prime_W(R_prime_W), .RES(RES_prime), .CS(A), .OUT(A_out),
    .MSB(A_msb));
  Pull_Resistor pull_resistor_1 (.node(A_out));
  right_shift_register u_B (
    .IN(IN), .SHIFT(decoder_1_out7), .CLK(CLK), .R_prime_W(R_prime_W), .RES(RES_prime), .CS(B), .OUT(B_out),
    .LSB(B_lsb));
  Pull_Resistor pull_resistor_2 (.node(B_out));
  assign controlled_buffer_1_out = decoder_1_out0 ? ADD_out : 16'bz;  // Controlled_Buffer controlled_buffer_1
  adder16 ADD (.IN1(B_out), .CI(FLAGS[7]), .IN2(A_out), .OUT(ADD_out), .CO(ADD_co));
  adder16 SUB (.IN1(A_out), .CI(1'b1), .IN2(not_1_out), .OUT(SUB_out), .CO(SUB_co));
  assign not_1_out = ~B_out;  // NOT_Gate not_1, 16 bits wide
  and16 AND (.IN1(B_out), .IN2(A_out), .OUT(AND_out));
  or16 OR (.IN1(B_out), .IN2(A_out), .OUT(OR_out));
  xor16 XOR (.IN1(B_out), .IN2(A_out), .OUT(XOR_out));
  assign pull_resistor_3_node[7] = decoder_1_out0 ? ADD_co : 1'bz;  // Controlled_Buffer controlled_buffer_2
  assign controlled_buffer_1_out = decoder_1_out1 ? SUB_out : 16'bz;  // Controlled_Buffer controlled_buffer_3
  assign pull_resistor_3_node[7] = decoder_1_out1 ? SUB_co : 1'bz;  // Controlled_Buffer controlled_buffer_4
  assign controlled_buffer_1_out = decoder_1_out2 ? AND_out : 16'bz;  // Controlled_Buffer controlled_buffer_5
  assign controlled_buffer_1_out = decoder_1_out3 ? OR_out : 16'bz;  // Controlled_Buffer controlled_buffer_6
  assign controlled_buffer_1_out = decoder_1_out4 ? XOR_out : 16'bz;  // Controlled_Buffer controlled_buffer_7
  assign controlled_buffer_1_out = decoder_1_out5 ? ~A_out : 16'bz;  // Controlled_Inverter controlled_inverter_1
  assign controlled_buffer_1_out = decoder_1_out7 ? B_out : 16'bz;  // Controlled_Buffer controlled_buffer_8
  assign controlled_buffer_1_out = decoder_1_out6 ? A_out : 16'bz;  // Controlled_Buffer controlled_buffer_9
  LED LSB__B (.in(B_lsb));
  LED MSB__A (.in(A_msb));
  assign OUT = CLK ? controlled_buffer_1_out : 16'bz;  // Controlled_Buffer controlled_buffer_10
  Pull_Resistor pull_resistor_3 (.node(pull_resistor_3_node));
  or or_2 (or_2_out, ~R_prime_W, F);  // OR_Gate
  register8 register8_1 (.IN(pull_resistor_3_node), .CLK(CLK), .WE(F), .RES(RES_prime), .CS(or_2_out), .OUT(FLAGS));
endmodule

module adder16 (
  input  [15:0] IN1,
  input  CI,
  input  [15:0] IN2,
  output [15:0] OUT,
  output CO
);

  wire adder_1_co, adder_2_co, adder_3_co, adder_4_co, adder_5_co, adder_6_co, adder_7_co, adder_8_co,
       adder_9_co, adder_10_co, adder_11_co, adder_12_co, adder_13_co, adder_14_co, adder_15_co;

  adder adder_1 (.CI(CI), .B1(IN1[0]), .B2(IN2[0]), .Q1(OUT[0]), .CO(adder_1_co));
  adder adder_2 (.CI(adder_1_co), .B1(IN1[1]), .B2(IN2[1]), .Q1(OUT[1]), .CO(adder_2_co));
  adder adder_3 (.CI(adder_2_co), .B1(IN1[2]), .B2(IN2[2]), .Q1(OUT[2]), .CO(adder_3_co));
  adder adder_4 (.CI(adder_3_co), .B1(IN1[3]), .B2(IN2[3]), .Q1(OUT[3]), .CO(adder_4_co));
  adder adder_5 (.CI(adder_4_co), .B1(IN1[4]), .B2(IN2[4]), .Q1(OUT[4]), .CO(adder_5_co));
  adder adder_6 (.CI(adder_5_co), .B1(IN1[5]), .B2(IN2[5]), .Q1(OUT[5]), .CO(adder_6_co));
  adder adder_7 (.CI(adder_6_co), .B1(IN1[6]), .B2(IN2[6]), .Q1(OUT[6]), .CO(adder_7_co));
  adder adder_8 (.CI(adder_7_co), .B1(IN1[7]), .B2(IN2[7]), .Q1(OUT[7]), .CO(adder_8_co));
  adder adder_9 (.CI(adder_8_co), .B1(IN1[8]), .B2(IN2[8]), .Q1(OUT[8]), .CO(adder_9_co));
  adder adder_10 (.CI(adder_9_co), .B1(IN1[9]), .B2(IN2[9]), .Q1(OUT[9]), .CO(adder_10_co));
  adder adder_11 (.CI(adder_10_co), .B1(IN1[10]), .B2(IN2[10]), .Q1(OUT[10]), .CO(adder_11_co));
  adder adder_12 (.CI(adder_11_co), .B1(IN1[11]), .B2(IN2[11]), .Q1(OUT[11]), .CO(adder_12_co));
  adder adder_13 (.CI(adder_12_co), .B1(IN1[12]), .B2(IN2[12]), .Q1(OUT[12]), .CO(adder_13_co));
  adder adder_14 (.CI(adder_13_co), .B1(IN1[13]), .B2(IN2[13]), .Q1(OUT[13]), .CO(adder_14_co));
  adder adder_15 (.CI(adder_14_co), .B1(IN1[14]), .B2(IN2[14]), .Q1(OUT[14]), .CO(adder_15_co));
  adder adder_16 (.CI(adder_15_co), .B1(IN1[15]), .B2(IN2[15]), .Q1(OUT[15]), .CO(CO));
endmodule

module adder (
  input  CI,
  input  B1,
  input  B2,
  output Q1,
  output CO
);

  wire and_1_out, and_2_out, xor_1_out;

  xor xor_1 (xor_1_out, B1, B2);
  and and_1 (and_1_out, CI, xor_1_out);
  and and_2 (and_2_out, B2, B1);
  or or_1 (CO, and_1_out, and_2_out);
  xor xor_2 (Q1, CI, xor_1_out);
endmodule

module register16 (
  input  [15:0] IN,
  input  CLK,
  input  R_prime_W,
  input  RES,
  input  CS,
  output [15:0] OUT
);

  wire and_1_out, and_2_out, and_3_out, not_1_out;
  wire [15:0] register_1_q;

  and and_1 (and_1_out, CLK, CS);
  not not_1 (not_1_out, RES);
  and and_2 (and_2_out, and_1_out, R_prime_W);
  Register #(.width(16)) register_1 (.D(IN), .en(CS), .Q(register_1_q), .clk(and_2_out), .clr(not_1_out));
  assign OUT = and_3_out ? register_1_q : 16'bz;  // Controlled_Buffer controlled_buffer_1
  and and_3 (and_3_out, and_1_out, ~R_prime_W);  // AND_Gate

  // Notes on the sheet:
  //   OUT: pull=down
endmodule

module register8 (
  input  [7:0] IN,
  input  CLK,
  input  WE,
  input  RES,
  input  CS,
  output [7:0] OUT
);

  wire and_1_out, and_2_out, and_3_out, not_1_out;
  wire [7:0] register_1_q;

  and and_1 (and_1_out, CLK, CS);
  not not_1 (not_1_out, RES);
  and and_2 (and_2_out, and_1_out, WE);
  Register register_1 (.D(IN), .en(CS), .Q(register_1_q), .clk(and_2_out), .clr(not_1_out));
  assign OUT = and_3_out ? register_1_q : 8'bz;  // Controlled_Buffer controlled_buffer_1
  and and_3 (and_3_out, and_1_out, ~WE);  // AND_Gate

  // Notes on the sheet:
  //   OUT: pull=down
endmodule

module and16 (
  input  [15:0] IN1,
  input  [15:0] IN2,
  output [15:0] OUT
);

  and and_1 (OUT[9], IN1[9], IN2[9]);
  and and_2 (OUT[10], IN1[10], IN2[10]);
  and and_3 (OUT[11], IN1[11], IN2[11]);
  and and_4 (OUT[14], IN1[14], IN2[14]);
  and and_5 (OUT[15], IN1[15], IN2[15]);
  and and_6 (OUT[7], IN1[7], IN2[7]);
  and and_7 (OUT[8], IN1[8], IN2[8]);
  and and_8 (OUT[12], IN1[12], IN2[12]);
  and and_9 (OUT[13], IN1[13], IN2[13]);
  and and_10 (OUT[4], IN1[4], IN2[4]);
  and and_11 (OUT[5], IN1[5], IN2[5]);
  and and_12 (OUT[6], IN1[6], IN2[6]);
  and and_13 (OUT[1], IN1[1], IN2[1]);
  and and_14 (OUT[2], IN1[2], IN2[2]);
  and and_15 (OUT[3], IN1[3], IN2[3]);
  and and_16 (OUT[0], IN1[0], IN2[0]);
endmodule

module or16 (
  input  [15:0] IN1,
  input  [15:0] IN2,
  output [15:0] OUT
);

  or or_1 (OUT[10], IN1[10], IN2[10]);
  or or_2 (OUT[11], IN1[11], IN2[11]);
  or or_3 (OUT[15], IN1[15], IN2[15]);
  or or_4 (OUT[8], IN1[8], IN2[8]);
  or or_5 (OUT[9], IN1[9], IN2[9]);
  or or_6 (OUT[12], IN1[12], IN2[12]);
  or or_7 (OUT[13], IN1[13], IN2[13]);
  or or_8 (OUT[14], IN1[14], IN2[14]);
  or or_9 (OUT[5], IN1[5], IN2[5]);
  or or_10 (OUT[6], IN1[6], IN2[6]);
  or or_11 (OUT[7], IN1[7], IN2[7]);
  or or_12 (OUT[2], IN1[2], IN2[2]);
  or or_13 (OUT[3], IN1[3], IN2[3]);
  or or_14 (OUT[4], IN1[4], IN2[4]);
  or or_15 (OUT[0], IN1[0], IN2[0]);
  or or_16 (OUT[1], IN1[1], IN2[1]);
endmodule

module xor16 (
  input  [15:0] IN1,
  input  [15:0] IN2,
  output [15:0] OUT
);

  xor xor_1 (OUT[11], IN1[11], IN2[11]);
  xor xor_2 (OUT[15], IN1[15], IN2[15]);
  xor xor_3 (OUT[8], IN1[8], IN2[8]);
  xor xor_4 (OUT[9], IN1[9], IN2[9]);
  xor xor_5 (OUT[10], IN1[10], IN2[10]);
  xor xor_6 (OUT[12], IN1[12], IN2[12]);
  xor xor_7 (OUT[13], IN1[13], IN2[13]);
  xor xor_8 (OUT[14], IN1[14], IN2[14]);
  xor xor_9 (OUT[5], IN1[5], IN2[5]);
  xor xor_10 (OUT[6], IN1[6], IN2[6]);
  xor xor_11 (OUT[7], IN1[7], IN2[7]);
  xor xor_12 (OUT[3], IN1[3], IN2[3]);
  xor xor_13 (OUT[4], IN1[4], IN2[4]);
  xor xor_14 (OUT[0], IN1[0], IN2[0]);
  xor xor_15 (OUT[1], IN1[1], IN2[1]);
  xor xor_16 (OUT[2], IN1[2], IN2[2]);
endmodule

module shift_register16 (
  input  [15:0] IN,
  input  SHIFT,
  input  CLK,
  input  R_prime_W,
  input  RES,
  input  CS,
  output [15:0] OUT,
  output MSB
);

  wire and_1_out, and_2_out, not_1_out, not_2_out, not_3_out;
  wire [15:0] shift_register_1_q0;

  and and_1 (and_1_out, not_2_out, SHIFT);
  Shift_Register #(.length(16)) shift_register_1 (
    .shift(and_1_out), .in(1'b0), .clk(and_2_out), .out(MSB), .load(not_3_out), .clr(not_1_out), .d0(IN[0]),
    .q0(shift_register_1_q0[0]), .d1(IN[1]), .q1(shift_register_1_q0[1]), .d2(IN[2]),
    .q2(shift_register_1_q0[2]), .d3(IN[3]), .q3(shift_register_1_q0[3]), .d4(IN[4]),
    .q4(shift_register_1_q0[4]), .d5(IN[5]), .q5(shift_register_1_q0[5]), .d6(IN[6]),
    .q6(shift_register_1_q0[6]), .d7(IN[7]), .q7(shift_register_1_q0[7]), .d8(IN[8]),
    .q8(shift_register_1_q0[8]), .d9(IN[9]), .q9(shift_register_1_q0[9]), .d10(IN[10]),
    .q10(shift_register_1_q0[10]), .d11(IN[11]), .q11(shift_register_1_q0[11]), .d12(IN[12]),
    .q12(shift_register_1_q0[12]), .d13(IN[13]), .q13(shift_register_1_q0[13]), .d14(IN[14]),
    .q14(shift_register_1_q0[14]), .d15(IN[15]), .q15(shift_register_1_q0[15]));
  and and_2 (and_2_out, CLK, CS);
  not not_1 (not_1_out, RES);
  not not_2 (not_2_out, R_prime_W);
  assign OUT = not_2_out ? shift_register_1_q0 : 16'bz;  // Controlled_Buffer controlled_buffer_1
  not not_3 (not_3_out, not_2_out);

  // Notes on the sheet:
  //   OUT: pull=down
endmodule

module right_shift_register (
  input  [15:0] IN,
  input  SHIFT,
  input  CLK,
  input  R_prime_W,
  input  RES,
  input  CS,
  output [15:0] OUT,
  output LSB
);

  wire and_1_out, and_2_out, not_1_out, not_2_out, not_3_out;
  wire [15:0] shift_register_1_q15;

  and and_1 (and_1_out, not_2_out, SHIFT);
  Shift_Register #(.length(16)) shift_register_1 (
    .shift(and_1_out), .in(1'b0), .clk(and_2_out), .out(LSB), .load(not_3_out), .clr(not_1_out), .d0(IN[15]),
    .q0(shift_register_1_q15[15]), .d1(IN[14]), .q1(shift_register_1_q15[14]), .d2(IN[13]),
    .q2(shift_register_1_q15[13]), .d3(IN[12]), .q3(shift_register_1_q15[12]), .d4(IN[11]),
    .q4(shift_register_1_q15[11]), .d5(IN[10]), .q5(shift_register_1_q15[10]), .d6(IN[9]),
    .q6(shift_register_1_q15[9]), .d7(IN[8]), .q7(shift_register_1_q15[8]), .d8(IN[7]),
    .q8(shift_register_1_q15[7]), .d9(IN[6]), .q9(shift_register_1_q15[6]), .d10(IN[5]),
    .q10(shift_register_1_q15[5]), .d11(IN[4]), .q11(shift_register_1_q15[4]), .d12(IN[3]),
    .q12(shift_register_1_q15[3]), .d13(IN[2]), .q13(shift_register_1_q15[2]), .d14(IN[1]),
    .q14(shift_register_1_q15[1]), .d15(IN[0]), .q15(shift_register_1_q15[0]));
  and and_2 (and_2_out, CLK, CS);
  not not_1 (not_1_out, RES);
  not not_2 (not_2_out, R_prime_W);
  assign OUT = not_2_out ? shift_register_1_q15 : 16'bz;  // Controlled_Buffer controlled_buffer_1
  not not_3 (not_3_out, not_2_out);

  // Notes on the sheet:
  //   OUT: pull=down
endmodule
