// Logisim project mycpu.circ as structural Verilog: 6 circuits, main circuit main
module main (
  input  RES,
  input  [31:0] CONTROL_WORD,
  input  [15:0] Data_In,
  output [31:0] ADDR,
  output [15:0] Data_Out
);

  wire CLK_clk, not_1_out;
  wire [15:0] CIR_out;
  wire [31:0] control_unit_1_control_word;

  DotMatrix #(.matrixcols(32), .matrixrows(1)) dotmatrix_1 (
    .col0(control_unit_1_control_word[31]), .col1(control_unit_1_control_word[30]),
    .col2(control_unit_1_control_word[29]), .col3(control_unit_1_control_word[28]),
    .col4(control_unit_1_control_word[27]), .col5(control_unit_1_control_word[26]),
    .col6(control_unit_1_control_word[25]), .col7(control_unit_1_control_word[24]),
    .col8(control_unit_1_control_word[23]), .col9(control_unit_1_control_word[22]),
    .col10(control_unit_1_control_word[21]), .col11(control_unit_1_control_word[20]),
    .col12(control_unit_1_control_word[19]), .col13(control_unit_1_control_word[18]),
    .col14(control_unit_1_control_word[17]), .col15(control_unit_1_control_word[16]),
    .col16(control_unit_1_control_word[15]), .col17(control_unit_1_control_word[14]),
    .col18(control_unit_1_control_word[13]), .col19(control_unit_1_control_word[12]),
    .col20(control_unit_1_control_word[11]), .col21(control_unit_1_control_word[10]),
    .col22(control_unit_1_control_word[9]), .col23(control_unit_1_control_word[8]),
    .col24(control_unit_1_control_word[7]), .col25(control_unit_1_control_word[6]),
    .col26(control_unit_1_control_word[5]), .col27(control_unit_1_control_word[4]),
    .col28(control_unit_1_control_word[3]), .col29(control_unit_1_control_word[2]),
    .col30(control_unit_1_control_word[1]), .col31(control_unit_1_control_word[0]));
  Clock CLK (.HLT_prime(control_unit_1_control_word[0]), .CLK(CLK_clk));
  not not_1 (not_1_out, CLK_clk);
  Control_Unit control_unit_1 (.CONTROL_WORD(control_unit_1_control_word), .CLK(not_1_out), .Instruction(CIR_out));
  DotMatrix #(.matrixcols(16), .matrixrows(1)) dotmatrix_2 (
    .col0(Data_In[15]), .col1(Data_In[14]), .col2(Data_In[13]), .col3(Data_In[12]), .col4(Data_In[11]),
    .col5(Data_In[10]), .col6(Data_In[9]), .col7(Data_In[8]), .col8(Data_In[7]), .col9(Data_In[6]),
    .col10(Data_In[5]), .col11(Data_In[4]), .col12(Data_In[3]), .col13(Data_In[2]), .col14(Data_In[1]),
    .col15(Data_In[0]));
  Counter PC (
    .Data(Data_In), .OP(control_unit_1_control_word[8:7]), .EN(control_unit_1_control_word[9]),
    .CLK(CLK_clk), .RES(RES), .Value(ADDR[15:0]));  // open: CARRY
  _16bit_Register PR (
    .IN(Data_In), .CLK(CLK_clk), .R_prime_W(control_unit_1_control_word[1]), .RES(RES),
    .CS(control_unit_1_control_word[10]), .OUT(ADDR[31:16]));
  _16bit_Register CIR (
    .IN(Data_In), .CLK(CLK_clk), .R_prime_W(control_unit_1_control_word[1]), .RES(RES),
    .CS(control_unit_1_control_word[11]), .OUT(CIR_out));
  DotMatrix #(.matrixcols(16), .matrixrows(1)) dotmatrix_3 (
    .col0(Data_Out[15]), .col1(Data_Out[14]), .col2(Data_Out[13]), .col3(Data_Out[12]), .col4(Data_Out[11]),
    .col5(Data_Out[10]), .col6(Data_Out[9]), .col7(Data_Out[8]), .col8(Data_Out[7]), .col9(Data_Out[6]),
    .col10(Data_Out[5]), .col11(Data_Out[4]), .col12(Data_Out[3]), .col13(Data_Out[2]), .col14(Data_Out[1]),
    .col15(Data_Out[0]));
  DotMatrix #(.matrixcols(32), .matrixrows(1)) dotmatrix_4 (
    .col0(ADDR[31]), .col1(ADDR[30]), .col2(ADDR[29]), .col3(ADDR[28]), .col4(ADDR[27]), .col5(ADDR[26]),
    .col6(ADDR[25]), .col7(ADDR[24]), .col8(ADDR[23]), .col9(ADDR[22]), .col10(ADDR[21]), .col11(ADDR[20]),
    .col12(ADDR[19]), .col13(ADDR[18]), .col14(ADDR[17]), .col15(ADDR[16]), .col16(ADDR[15]),
    .col17(ADDR[14]), .col18(ADDR[13]), .col19(ADDR[12]), .col20(ADDR[11]), .col21(ADDR[10]),
    .col22(ADDR[9]), .col23(ADDR[8]), .col24(ADDR[7]), .col25(ADDR[6]), .col26(ADDR[5]), .col27(ADDR[4]),
    .col28(ADDR[3]), .col29(ADDR[2]), .col30(ADDR[1]), .col31(ADDR[0]));
  Registers Register_Block (
    .Reset(RES), .Clock(CLK_clk), .R_prime_W(control_unit_1_control_word[1]), .Data(Data_In),
    .Output(Data_Out), .Reg_Access(control_unit_1_control_word[2]),
    .Reg_Select(control_unit_1_control_word[6:3]));
endmodule

module _16bit_Register (
  input  [15:0] IN,
  input  CLK,
  input  R_prime_W,
  input  RES,
  input  CS,
  output [15:0] OUT
);

  wire and_1_out, and_2_out, not_1_out;
  wire [15:0] register_1_q;

  and and_1 (and_1_out, CLK, CS);
  not not_1 (not_1_out, RES);
  assign OUT = and_2_out ? register_1_q : 16'bz;  // Controlled_Buffer controlled_buffer_1
  Register #(.width(16)) register_1 (.D(IN), .en(CS), .Q(register_1_q), .clk(and_1_out), .clr(not_1_out));
  and and_2 (and_2_out, and_1_out, ~R_prime_W);  // AND_Gate

  // Notes on the sheet:
  //   OUT: pull=down
endmodule

module Registers (
  input  Reset,
  input  Clock,
  input  R_prime_W,
  input  Reg_Access,
  input  [3:0] Reg_Select,
  input  [15:0] Data,
  output [15:0] Output
);

  wire decoder_1_out0, decoder_1_out1, decoder_1_out2, decoder_1_out3, decoder_1_out4, decoder_1_out5,
       decoder_1_out6, decoder_1_out7, decoder_1_out8, decoder_1_out9, decoder_1_out10, decoder_1_out11,
       decoder_1_out12, decoder_1_out13, decoder_1_out14, decoder_1_out15;

  Decoder #(.select(4), .disabled(0)) decoder_1 (
    .out0(decoder_1_out0), .out1(decoder_1_out1), .out2(decoder_1_out2), .out3(decoder_1_out3),
    .out4(decoder_1_out4), .out5(decoder_1_out5), .out6(decoder_1_out6), .out7(decoder_1_out7),
    .out8(decoder_1_out8), .out9(decoder_1_out9), .out10(decoder_1_out10), .out11(decoder_1_out11),
    .out12(decoder_1_out12), .out13(decoder_1_out13), .out14(decoder_1_out14), .out15(decoder_1_out15),
    .sel(Reg_Select), .en(Reg_Access));
  _16bit_Register r0 (.IN(Data), .CLK(Clock), .R_prime_W(R_prime_W), .RES(Reset), .CS(decoder_1_out0), .OUT(Output));
  _16bit_Register r8 (.IN(Data), .CLK(Clock), .R_prime_W(R_prime_W), .RES(Reset), .CS(decoder_1_out8), .OUT(Output));
  _16bit_Register r1 (.IN(Data), .CLK(Clock), .R_prime_W(R_prime_W), .RES(Reset), .CS(decoder_1_out1), .OUT(Output));
  _16bit_Register r9 (.IN(Data), .CLK(Clock), .R_prime_W(R_prime_W), .RES(Reset), .CS(decoder_1_out9), .OUT(Output));
  _16bit_Register r2 (.IN(Data), .CLK(Clock), .R_prime_W(R_prime_W), .RES(Reset), .CS(decoder_1_out2), .OUT(Output));
  _16bit_Register r10 (.IN(Data), .CLK(Clock), .R_prime_W(R_prime_W), .RES(Reset), .CS(decoder_1_out10), .OUT(Output));
  _16bit_Register r3 (.IN(Data), .CLK(Clock), .R_prime_W(R_prime_W), .RES(Reset), .CS(decoder_1_out3), .OUT(Output));
  _16bit_Register r11 (.IN(Data), .CLK(Clock), .R_prime_W(R_prime_W), .RES(Reset), .CS(decoder_1_out11), .OUT(Output));
  _16bit_Register r4 (.IN(Data), .CLK(Clock), .R_prime_W(R_prime_W), .RES(Reset), .CS(decoder_1_out4), .OUT(Output));
  _16bit_Register r12 (.IN(Data), .CLK(Clock), .R_prime_W(R_prime_W), .RES(Reset), .CS(decoder_1_out12), .OUT(Output));
  _16bit_Register r5 (.IN(Data), .CLK(Clock), .R_prime_W(R_prime_W), .RES(Reset), .CS(decoder_1_out5), .OUT(Output));
  _16bit_Register r13 (.IN(Data), .CLK(Clock), .R_prime_W(R_prime_W), .RES(Reset), .CS(decoder_1_out13), .OUT(Output));
  _16bit_Register r6 (.IN(Data), .CLK(Clock), .R_prime_W(R_prime_W), .RES(Reset), .CS(decoder_1_out6), .OUT(Output));
  _16bit_Register r14 (.IN(Data), .CLK(Clock), .R_prime_W(R_prime_W), .RES(Reset), .CS(decoder_1_out14), .OUT(Output));
  _16bit_Register r7 (.IN(Data), .CLK(Clock), .R_prime_W(R_prime_W), .RES(Reset), .CS(decoder_1_out7), .OUT(Output));
  _16bit_Register r15 (.IN(Data), .CLK(Clock), .R_prime_W(R_prime_W), .RES(Reset), .CS(decoder_1_out15), .OUT(Output));
endmodule

module Clock (
  input  HLT_prime,
  output CLK
);

  wire clock_1_out;

  Pull_Resistor pull_resistor_1 (.node(HLT_prime));
  Clock_part clock_1 (.out(clock_1_out));
  and and_1 (CLK, HLT_prime, clock_1_out);
endmodule

module Counter (
  input  [15:0] Data,
  input  CARRY,
  input  [1:0] OP,
  input  EN,
  input  CLK,
  input  RES,
  output [15:0] Value
);

  wire and_1_out, and_2_out, decoder_1_out0, decoder_1_out1, decoder_1_out2, decoder_1_out3, not_1_out,
       or_1_out, or_2_out, or_3_out;

  Decoder #(.select(2), .disabled(0)) decoder_1 (
    .out0(decoder_1_out0), .out1(decoder_1_out1), .out2(decoder_1_out2), .out3(decoder_1_out3), .sel(OP),
    .en(EN));
  or or_1 (or_1_out, decoder_1_out2, decoder_1_out3);
  Pull_Resistor pull_resistor_1 (.node(or_1_out));
  Pull_Resistor pull_resistor_2 (.node(decoder_1_out1));
  or or_2 (or_2_out, decoder_1_out3, decoder_1_out1);
  Counter_part #(.width(16), .max('hffff)) counter_1 (
    .load(or_2_out), .D(Data), .count(or_1_out), .Q(Value), .carry(CARRY), .clk(and_2_out), .clr(or_3_out));
  or or_3 (or_3_out, and_1_out, not_1_out);
  and and_1 (and_1_out, decoder_1_out0, and_2_out);
  not not_1 (not_1_out, RES);
  and and_2 (and_2_out, EN, CLK);
endmodule

module Control_Unit (
  input  [15:0] Instruction,
  input  CLK,
  output [31:0] CONTROL_WORD
);

  wire [3:0] counter_1_q;

  Counter_part #(.width(4), .max('hf)) counter_1 (
    .load(1'b0), .D(4'b0000), .count(1'b1), .Q(counter_1_q), .clk(CLK), .clr(counter_1_q[3]));  // open: carry
  ROM #(.addrWidth(20), .dataWidth(32)) rom_1 (.addr({Instruction, counter_1_q}), .data(CONTROL_WORD));  // open: sel
endmodule
